# Fritzing sketch HC-05 connection (saved by Fritzing 0.9.3b)
breadboards: 1

parts:
  Part1 = Bluetooth HC-05 Macho
  Part2 = Arduino Nano (Rev3.0)

nets:
  N1: Part1.TXD, Part2.D5
  N2: Part1.RXD, Part2.D6
  VCC: Part1.VCC, Part2.5V
  GND: Part1.GND, Part2.GND
