# Fritzing sketch L298N Motor Driver (saved by Fritzing 0.9.3b)
breadboards: 1

parts:
  L298N1 = L298N DC motor driver
  Part1 = Arduino Uno (Rev3)
  Part2 = Thumb Joystick
  M1 = DC Motor  # not connected
  M2 = DC Motor  # not connected
  U2 = LIPO-2000mAh [package=lipo-2000]

nets:
  N1: L298N1.ENA, Part1.D9_PWM
  N2: L298N1.ENB, Part1.D3_PWM
  N3: L298N1.IN1, Part1.D7
  N4: L298N1.IN2, Part1.D6_PWM
  N5: L298N1.IN3, Part1.D5_PWM
  N6: L298N1.IN4, Part1.D4
  N7: Part1.A0, Part2.VERT
  N8: Part1.A1, Part2.HORZ
  GND: Part1.GND, Part2.GND, U2.-
  VIN: Part1.VIN, Part2.VCC

custom parts:
  L298N DC motor driver: 2x DC motor driver with 78M05 positive voltage regulator (7..35 V) L298N: max 46 V, 2 A Set 5 V Enable jumper to enable 5 V regultor (needed for the L298N) and +5 V output at screw terminal or supply external +5 V at screw terminal Set ENA and/or ENB to +5 V to enable motor permanently or supply ENA and/or ENB with PWM signal IN1 and IN2 set rotation directory for motor A (OUT1/OUT2) IN2 and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
