# Fritzing sketch Motor driver with relays (saved by Fritzing 0.9.3b)
breadboards: 1

parts:
  OMRON1 = OMRON PCB Power Relay – G5LE [part_number="G5LE-1\n" package=THT]
  OMRON2 = OMRON PCB Power Relay – G5LE [part_number="G5LE-1\n" package=THT]
  U1 = LIPO-2000mAh [package=lipo-2000]
  M1 = DC Motor  # not connected

nets:
  N1: OMRON1.A, OMRON2.A, U1.+
  N2: OMRON1.B, OMRON2.B, U1.-
