# Fritzing sketch Relay connection (saved by Fritzing 0.9.3b)
breadboards: 1

parts:
  OMRON1 = OMRON PCB Power Relay – G5LE [part_number="G5LE-1\n" package=THT]
  Q1 = NPN-Transistor [package="TO92 [THT]"]
  Part1 = Arduino Uno (Rev3)
  R1 = Resistor [tolerance=±5% resistance=470 package="0402 [SMD]"]
  LED1 = LEDs [package=led10mm]
  D1 = Rectifier Diode [part_number=1N4001 package="300 mil [THT]"]

nets:
  N1: OMRON1.COIL1, Q1.C
  N2: OMRON1.C, LED1.C, D1.anode
  N3: OMRON1.COIL2, Part1.5V, D1.cathode
  N4: Q1.E, Part1.GND
  N5: Q1.B, R1.Pin_1
  N6: Part1.D13/SCK, R1.Pin_0

notes:
  AC

custom parts:
  LEDs: LEDs Standard schematic elements and footprints for 5mm, 3mm, 1206, and 0603 sized LEDs. 5mm - Spark Fun Electronics SKU : COM-00529 (and others)
