# Fritzing sketch USB HID with pro micro (saved by Fritzing 0.9.3b)
breadboards: 1

parts:
  Part1 = Arduino Pro Micro (Clone)
  Part2 = Thumb Joystick
  S1 = Momentary Switch [package=ksa_sealed_tac_switch]
  R1 = Resistor [tolerance=±5% resistance=10k package="2512 [SMD]"]

nets:
  GND: Part1.GND, Part2.GND, R1.Pin_1
  N1: Part1.D2, S1.2, R1.Pin_0
  N2: Part1.A0, Part2.HORZ
  N3: Part1.A1, Part2.VERT
  N4: Part1.RAW, Part2.VCC, S1.4
