# Fritzing sketch driving Motor with Arduino (saved by Fritzing 0.9.3b)
breadboards: 1

parts:
  Part1 = Arduino Uno (Rev3) - ICSP
  Q1 = NPN-Transistor [part_number=BC547 package="TO92 [THT]"]
  M1 = DC Motor
  D2 = Rectifier Diode [part_number=1N4007 package="Melf DO-213 AB [SMD]"]
  R1 = Resistor [tolerance=±5% resistance=220 package="0805 [SMD]"]

nets:
  N1: Part1.D11_PWM/MOSI, R1.Pin_0
  N2: Part1.GND, Q1.E, M1.pin_2
  N3: Part1.5V, M1.pin_1, D2.cathode
  N4: Q1.B, R1.Pin_1
  N5: Q1.C, D2.anode
