# Fritzing sketch motor driver circuit (saved by Fritzing 0.9.3b)
breadboards: 1

parts:
  Part1 = Arduino Uno (Rev3)
  R1 = Resistor [tolerance=±0.5% resistance=470 package="2512 [SMD]"]
  M1 = DC Motor
  Q1 = NPN-Transistor [package="TO92 [THT]"]
  D1 = Diode [package=diode-1n4001]

nets:
  N1: Part1.D11_PWM/MOSI, R1.Pin_0
  N2: Part1.GND, Q1.E
  N3: R1.Pin_1, Q1.B
  N4: M1.pin_2, Q1.C, D1.A
