# Fritzing sketch nRFl01 testing (saved by Fritzing 0.9.3b)

parts:
  Part3 = NRF24L01+ Breakout Board
  Part4 = Arduino Nano (Rev3.0)
  C2 = Capacitor Polarized [package=cpol-radial-100uf-25v]
  U4 = V_REG_LD1117VXX [package=78xxl]
  J1 = double row male pin header, 8 pins [form="♂ (male)"]

nets:
  GND: Part3.GND, Part4.GND, Part4.RESET, C2.-, U4.GND, J1.pin2
  N1: Part3.VCC, C2.+, U4.OUT
  N2: Part3.CE, Part4.D7
  N3: Part3.CS, Part4.D8
  N4: Part3.SCK, Part4.3V3, Part4.D13/SCK
  N5: Part3.MOSI, Part4.D10, Part4.D11/MOSI
  N6: Part3.MISO, Part4.D12/MISO
  N7: Part4.D2, J1.pin4
  N8: Part4.D3, J1.pin5
  N9: Part4.D4, J1.pin6
  N10: Part4.D5, J1.pin7
  N11: Part4.D6, J1.pin8
  N12: Part4.D9, J1.pin3
  N13: Part4.VIN, U4.IN, J1.pin1

notes:
  Reciever Schematic
  VCC
  GND
  D9
  D6
  D5
  D4
  D2
  D3
