# Fritzing sketch nrf based bot (saved by Fritzing 0.9.3b)

parts:
  Part1 = NRF24L01+ Breakout Board
  Part2 = Arduino Nano (Rev3.0)
  Part3 = Arduino Uno (Rev3)
  Part5 = Thumb Joystick
  Part6 = NRF24L01+ Breakout Board
  C1 = Capacitor Polarized [package=cpol-radial-100uf-25v]
  U1 = V_REG_LD1117VXX [package=78xxl]
  L298N1 = L298N DC motor driver
  C2 = Capacitor Polarized [package=cpol-radial-100uf-25v]
  U3 = V_REG_LD1117VXX [package=78xxl]
  VCC1 = Battery
  VCC2 = Battery
  VCC3 = Battery
  M1 = DC Motor
  M2 = DC Motor

nets:
  GND: Part1.GND, Part2.GND, C1.-, L298N1.GND, U3.GND, VCC3.-
  N1: Part1.VCC, C1.+, U3.OUT
  N2: Part1.CE, Part2.D7
  N3: Part1.CS, Part2.D8
  N4: Part1.SCK, Part2.D13/SCK
  N5: Part1.MOSI, Part2.D11/MOSI
  N6: Part1.MISO, Part2.D12/MISO
  N7: Part2.D2, L298N1.IN1
  N8: Part2.D3, L298N1.IN2
  N9: Part2.D4, L298N1.IN3
  N10: Part2.D5, L298N1.IN4
  N11: Part2.D6, L298N1.ENB
  N12: Part2.D9, L298N1.ENA
  VIN: Part2.VIN, L298N1.5V, U3.IN
  N13: Part3.A0, Part5.VERT
  N14: Part3.A1, Part5.HORZ
  N15: Part3.D8, Part6.CS
  N16: Part3.D11_PWM/MOSI, Part6.MOSI
  N17: Part3.D12/MISO, Part6.MISO
  N18: Part3.D13/SCK, Part6.SCK
  N19: Part3.D7, Part6.CE
  5V: Part3.5V, Part5.VCC
  GND_2: Part3.GND, Part5.GND, Part6.GND, U1.GND, C2.-
  N20: Part3.VIN, U1.IN
  N21: Part6.VCC, U1.OUT, C2.+
  N22: L298N1.OUT1, M1.pin_2
  N23: L298N1.OUT2, M1.pin_1
  N24: L298N1.OUT3, M2.pin_1
  N25: L298N1.OUT4, M2.pin_2
  N26: L298N1.12V, VCC1.+
  N27: VCC1.-, VCC2.+
  N28: VCC2.-, VCC3.+

notes:
  transmitter
  schematic
  Reciever Schematic

custom parts:
  L298N DC motor driver: 2x DC motor driver with 78M05 positive voltage regulator (7..35 V) L298N: max 46 V, 2 A Set 5 V Enable jumper to enable 5 V regultor (needed for the L298N) and +5 V output at screw terminal or supply external +5 V at screw terminal Set ENA and/or ENB to +5 V to enable motor permanently or supply ENA and/or ENB with PWM signal IN1 and IN2 set rotation directory for motor A (OUT1/OUT2) IN2 and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
