# Fritzing sketch portentionmeter Experiment (saved by Fritzing 0.9.3b)
breadboards: 1

parts:
  Part1 = Arduino Uno (Rev3) - ICSP
  R1 = Trimmer Potentiometer [maximum_resistance=10kΩ package=THT]
  LED1 = smd LED [color="Red (633nm)" package="1206 [SMD]"]
  R2 = Resistor [tolerance=±5% resistance=470 package="2010 [SMD]"]

nets:
  N1: Part1.A0, R1.wiper
  N2: Part1.D3_PWM, R2.Pin_1
  N3: Part1.5V, R1.leg1
  N4: Part1.GND, R1.leg2, LED1.cathode
  N5: LED1.anode, R2.Pin_0
