# Fritzing sketch pushButton Experiment (saved by Fritzing 0.9.3b)
breadboards: 1

parts:
  Part1 = Arduino Uno (Rev3)
  S1 = Pushbutton [package="[THT]"]
  R1 = Resistor [tolerance=±5% resistance=10k package="0603 [SMD]"]
  LED1 = smd LED [color="Red (633nm)" package="1206 [SMD]"]  # not connected
  R2 = Resistor [tolerance=±5% resistance=470 package="0603 [SMD]"]

nets:
  N1: Part1.D12/MISO, S1.Pin_3, S1.Pin_4, R1.Pin_1
  N2: Part1.D13/SCK, R2.Pin_0
  N3: Part1.5V, S1.Pin_1, S1.Pin_2
  N4: Part1.GND, R1.Pin_0
